# Fritzing sketch STAP (saved by Fritzing 0.9.0b)
breadboards: 2

parts:
  Composant1 = Arduino Uno (Rev3)
  LCD1 = LCD screen
  S1 = Pushbutton [package="[THT]"]
  S2 = Pushbutton [package="[THT]"]
  S3 = Pushbutton [package="[THT]"]
  LED1 = LED - 5mm [color="Red (633nm)" package="5 mm [THT]"]
  LED2 = LED - 5mm [color="Green (560nm)" package="5 mm [THT]"]
  J1 = Piezo Speaker
  R1 = Rotary Potentiometer (Small) [maximum_resistance=100kΩ package=THT]
  R4 = Resistor [tolerance=±5% resistance=220 package=THT]
  R5 = Resistor [tolerance=±5% resistance=10k package=THT]
  R6 = Resistor [tolerance=±5% resistance=220 package=THT]
  R7 = Resistor [tolerance=±5% resistance=10k package=THT]
  R8 = Resistor [tolerance=±5% resistance=10k package=THT]
  R9 = Resistor [tolerance=±5% resistance=220 package=THT]

nets:
  N1: Composant1.D8, LED1.anode
  N2: Composant1.D9_PWM, S2.Pin_3, S2.Pin_4, R7.Pin_0
  N3: Composant1.D10_PWM/SS, LED2.anode
  N4: Composant1.D11_PWM/MOSI, LCD1.E
  N5: Composant1.D12/MISO, LCD1.RS
  N6: Composant1.D13/SCK, S3.Pin_3, S3.Pin_4, R5.Pin_0
  N7: Composant1.D2, LCD1.DB7
  N8: Composant1.D3_PWM, LCD1.DB6
  N9: Composant1.D4, LCD1.DB5
  N10: Composant1.D5_PWM, LCD1.DB4
  N11: Composant1.D6_PWM, S1.Pin_3, S1.Pin_4, R8.Pin_0
  N12: Composant1.D7, J1.pin2
  5V: Composant1.5V, LCD1.VDD, S1.Pin_1, S1.Pin_2, S2.Pin_1, S2.Pin_2, S3.Pin_1, S3.Pin_2, R1.leg1, R9.Pin_0
  GND: Composant1.GND, LCD1.VSS, LCD1.R/W, LCD1.LED-, J1.pin1, R1.leg2, R4.Pin_1, R5.Pin_1, R6.Pin_1, R7.Pin_1, R8.Pin_1
  N13: LCD1.V0, R1.wiper
  N14: LCD1.LED+, R9.Pin_1
  N15: LED1.cathode, R6.Pin_0
  N16: LED2.cathode, R4.Pin_0
